# Fritzing sketch crane_game_fritzing (saved by Fritzing 1.0.7)
breadboards: 1

parts:
  L298N1 = L298N DC motor driver
  M1 = DC Motor [voltage_(max)=6V voltage_(min)=3V]
  JACK1 = 2.1mm Barrel Jack with Terminal Block
  L298N2 = L298N DC motor driver
  Part2 = Arduino Mega 2560 (Rev3)
  JL012-13-5_1 = JL012-13-5.2 Lever (Limit) Switch SPDT + NO + NC [part_number=JL012-13-5.2]
  JL012-13-5_2 = JL012-13-5.2 Lever (Limit) Switch SPDT + NO + NC [part_number=JL012-13-5.2]
  JL012-13-5_3 = JL012-13-5.2 Lever (Limit) Switch SPDT + NO + NC [part_number=JL012-13-5.2]
  JL012-13-5_4 = JL012-13-5.2 Lever (Limit) Switch SPDT + NO + NC [part_number=JL012-13-5.2]
  M5 = DC Motor [voltage_(max)=6V voltage_(min)=3V]
  U1 = SWITCH_SPDT [package=kps-1290]
  M4 = DC Motor [voltage_(max)=6V voltage_(min)=3V]

nets:
  N1: L298N1.OUT1, M4.pin_2
  N2: L298N1.OUT2, M4.pin_1
  N3: L298N1.OUT3, M1.pin_2
  N4: L298N1.OUT4, M1.pin_1
  12V: L298N1.12V, L298N2.12V, U1.P
  GND: L298N1.GND, JACK1.NEG, L298N2.GND, Part2.GND, JL012-13-5_1.C, JL012-13-5_2.C, JL012-13-5_3.C, JL012-13-5_4.C, U1.S
  N5: L298N1.IN1, Part2.D8_PWM
  N6: L298N1.IN2, Part2.D9_PWM
  N7: L298N1.IN3, Part2.D10_PWM
  N8: L298N1.IN4, Part2.D11_PWM
  N9: JACK1.POS, U1.O
  N10: L298N2.OUT3, M5.pin_2
  N11: L298N2.OUT4, M5.pin_1
  N12: L298N2.IN3, Part2.D12_PWM
  N13: L298N2.IN4, Part2.D13_PWM
  N14: Part2.D2_PWM, JL012-13-5_1.NC
  N15: Part2.D3_PWM, JL012-13-5_2.NC
  N16: Part2.D4_PWM, JL012-13-5_4.NC
  N17: Part2.D5_PWM, JL012-13-5_3.NC

notes:
  Power
  Y Direction Motor
  L298N Motor Driver Board
  Z Direction Motor
  Arduino MEGA
  On/Off Switch
  X Direction Motor
  Fwd Limit
  Back Limit
  Left Limit
  Right Limit

custom parts:
  L298N DC motor driver: 2x DC motor driver with 78M05 positive voltage regulator (7..35 V) L298N: max 46 V, 2 A Set 5 V Enable jumper to enable 5 V regultor (needed for the L298N) and +5 V output at screw terminal or supply external +5 V at screw terminal Set ENA and/or ENB to +5 V to enable motor permanently or supply ENA and/or ENB with PWM signal IN1 and IN2 set rotation directory for motor A (OUT1/OUT2) IN2 and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
  JL012-13-5.2 Lever (Limit) Switch SPDT + NO + NC: Micro Switch; Model No.: JL012-13.5-2; Actuator Action: Momentary; Actuator Type: Hinge Lever; Contact Configuration: 1NO, 1NC (SPDT) Temperature -25~65℃；Relative humidity: below 85%; Rate Voltage: 125V AC; Rated Current: 1A.
